# Fritzing sketch Chronometer_Group3 (saved by Fritzing 0.9.4)
breadboards: 1

parts:
  Part1 = Arduino Uno (Rev3)
  S1 = Pushbutton [package="[THT]"]

nets:
  N1: Part1.GND, S1.Pin_1, S1.Pin_2
  N2: Part1.D2, S1.Pin_3
